// Logisim project csg_examine.circ as structural Verilog: 1 circuit, main circuit main
module main (
);

  wire and_1_out, and_2_out, and_3_out, and_4_out, and_5_out, and_6_out, and_7_out, and_8_out, button_1_out,
       clock_1_out, d_ff_1_q, d_ff_1_qn, d_ff_2_q, d_ff_2_qn, d_ff_3_q, d_ff_3_qn, or_1_out, or_2_out,
       or_3_out, or_4_out, or_5_out;

  Button button_1 (.out(button_1_out));
  and and_1 (and_1_out, d_ff_2_q, d_ff_3_qn);
  and and_2 (and_2_out, d_ff_1_q, button_1_out);
  and and_3 (and_3_out, d_ff_2_q, d_ff_3_q);
  and and_4 (and_4_out, button_1_out, d_ff_3_qn);
  or or_1 (or_1_out, and_2_out, and_3_out);
  or or_2 (or_2_out, and_1_out, and_5_out);
  or or_3 (or_3_out, and_2_out, and_1_out, and_4_out);
  Clock clock_1 (.out(clock_1_out));
  D_Flip_Flop d_ff_1 (.clk(clock_1_out), .D(or_1_out), .Q(d_ff_1_q), .Qn(d_ff_1_qn));  // open: preset, en, reset
  D_Flip_Flop d_ff_2 (.clk(clock_1_out), .D(or_2_out), .Q(d_ff_2_q), .Qn(d_ff_2_qn));  // open: preset, en, reset
  D_Flip_Flop d_ff_3 (.clk(clock_1_out), .D(or_3_out), .Q(d_ff_3_q), .Qn(d_ff_3_qn));  // open: preset, en, reset
  and and_5 (and_5_out, d_ff_1_qn, d_ff_2_qn, d_ff_3_q);
  and and_6 (and_6_out, d_ff_1_qn, d_ff_2_qn);
  and and_7 (and_7_out, d_ff_2_qn, d_ff_3_q);
  LED led_1 (.in(and_5_out));
  LED led_2 (.in(or_4_out));
  or or_4 (or_4_out, and_6_out, and_7_out);
  or or_5 (or_5_out, d_ff_2_qn, d_ff_3_qn);
  LED led_3 (.in(or_5_out));
  and and_8 (and_8_out, d_ff_1_q, d_ff_3_qn);
  LED led_4 (.in(and_8_out));
endmodule
